// Logisim project ALU.circ as structural Verilog: 1 circuit, main circuit main
module main (
  input  [3:0] A,
  input  [3:0] _1,
  input  [3:0] B,
  input  [3:0] minus_1,
  input  S,
  input  S_2,
  output [3:0] out_7,
  output out_8
);

  wire and_1_out, not_1_out, not_2_out, not_3_out, not_4_out;
  wire [3:0] multiplexer_1_out;

  not not_1 (not_1_out, B[3]);
  not not_2 (not_2_out, B[1]);
  not not_3 (not_3_out, B[0]);
  not not_4 (not_4_out, B[2]);
  Multiplexer #(.select(2)) multiplexer_1 (
    .in0(_1[0]), .in1(B[0]), .in2(not_3_out), .in3(minus_1[0]), .out(multiplexer_1_out[0]), .sel({S, S_2}));  // open: en
  Multiplexer #(.select(2)) multiplexer_2 (
    .in0(_1[1]), .in1(B[1]), .in2(not_2_out), .in3(minus_1[1]), .out(multiplexer_1_out[1]), .sel({S, S_2}));  // open: en
  Multiplexer #(.select(2)) multiplexer_3 (
    .in0(_1[2]), .in1(B[2]), .in2(not_4_out), .in3(minus_1[2]), .out(multiplexer_1_out[2]), .sel({S, S_2}));  // open: en
  Multiplexer #(.select(2)) multiplexer_4 (
    .in0(_1[3]), .in1(B[3]), .in2(not_1_out), .in3(minus_1[3]), .out(multiplexer_1_out[3]), .sel({S, S_2}));  // open: en
  and and_1 (and_1_out, S, ~S_2);  // AND_Gate
  Adder #(.width(4)) adder_1 (.a(A), .b(multiplexer_1_out), .out(out_7), .cin(and_1_out), .cout(out_8));
endmodule
