// Logisim project car-signals.circ as structural Verilog: 1 circuit, main circuit main
module main (
  input  left,
  input  emergency,
  input  right,
  input  brake,
  output left_2,
  output right_2,
  output tail
);

  or or_1 (left_2, left, emergency);
  or or_2 (right_2, emergency, right);

  assign tail = brake;
endmodule
