// Logisim project car-signals.circ as structural Verilog: 1 circuit, main circuit main
module main (
  input  Left_Turn_Switch,
  input  Emergency_Switch,
  input  in_3,
  input  in_4,
  output Left_Turn_Signal,
  output out_6,
  output out_7,
  output out_8
);

  or or_1 (Left_Turn_Signal, Left_Turn_Switch, Emergency_Switch);
  or or_2 (out_6, Emergency_Switch, in_3);

  assign out_7 = in_4;
  assign out_8 = in_4;

  // Notes on the sheet:
  //   Brake
  //   Right Turn Switch
  //   Tail Lights
  //   Right Turn Signal
endmodule
