// Logisim project 3-bit-comparator.circ as structural Verilog: 1 circuit, main circuit main
module main (
  input  A2,
  input  B2,
  input  A1,
  input  B1,
  input  A0,
  input  B0,
  output B___A,
  output A___B,
  output equal
);

  wire and_1_out, and_2_out, and_3_out, and_4_out, and_5_out, and_6_out, nor_1_out, nor_2_out, nor_3_out,
       not_1_out, not_2_out, not_3_out, not_4_out, not_5_out, not_6_out;

  not not_1 (not_1_out, A2);
  not not_2 (not_2_out, B2);
  and and_1 (and_1_out, not_1_out, B2);
  and and_2 (and_2_out, A2, not_2_out);
  nor nor_1 (nor_1_out, and_1_out, and_2_out);
  not not_3 (not_3_out, A1);
  not not_4 (not_4_out, B1);
  and and_3 (and_3_out, nor_1_out, not_3_out, B1);
  and and_4 (and_4_out, A1, not_4_out, nor_1_out);
  nor nor_2 (nor_2_out, and_3_out, and_4_out);
  not not_5 (not_5_out, A0);
  not not_6 (not_6_out, B0);
  and and_5 (and_5_out, nor_2_out, nor_1_out, not_5_out, B0);
  and and_6 (and_6_out, A0, not_6_out, nor_2_out, nor_1_out);
  or or_1 (B___A, and_1_out, and_3_out, and_5_out);
  nor nor_3 (nor_3_out, and_5_out, and_6_out);
  not not_7 (A___B, B___A);
  and and_7 (equal, nor_2_out, nor_3_out, nor_1_out);

  // Notes on the sheet:
  //   3 bit Comparator
endmodule
