// Logisim project 4-1-multiplexer.circ as structural Verilog: 1 circuit, main circuit main
module main (
  input  in_1,
  input  in_2,
  input  in_3,
  input  in_4,
  input  [1:0] YZ,
  input  in_6,
  input  in_7,
  input  in_8,
  input  X,
  input  in_10,
  output out_11
);

  wire multiplexer_1_out, multiplexer_2_out;

  Multiplexer #(.select(2)) multiplexer_1 (
    .in0(in_1), .in1(in_2), .in2(in_3), .in3(in_4), .out(multiplexer_1_out), .sel(YZ));  // open: en
  Multiplexer #(.select(2)) multiplexer_2 (
    .in0(in_6), .in1(in_7), .in2(in_8), .in3(in_10), .out(multiplexer_2_out), .sel(YZ));  // open: en
  Multiplexer #(.select(2)) multiplexer_3 (
    .in0(multiplexer_1_out), .in1(multiplexer_1_out), .in2(multiplexer_2_out), .in3(multiplexer_2_out),
    .out(out_11), .sel({2{X}}));  // open: en

  // Notes on the sheet:
  //   4-to-1 Multiplexer
  //   Σ(1, 2, 4, 6, 7)
endmodule
