// Logisim project 8-1-multiplexer.circ as structural Verilog: 1 circuit, main circuit main
module main (
  input  [2:0] XYZ,
  input  in_2,
  input  in_3,
  input  in_4,
  input  in_5,
  input  in_6,
  input  in_7,
  input  in_8,
  input  in_9,
  output out_10
);

  Multiplexer #(.select(3)) multiplexer_1 (
    .in0(in_2), .in1(in_3), .in2(in_4), .in3(in_5), .in4(in_6), .in5(in_7), .in6(in_8), .in7(in_9),
    .out(out_10), .sel(XYZ));  // open: en

  // Notes on the sheet:
  //   8-to-1 Multiplexer
  //   Σ(1, 2, 4, 6, 7)
endmodule
