// Logisim project equal.circ as structural Verilog: 1 circuit, main circuit main
module main (
  input  ms,
  input  A,
  input  ls,
  input  in_4,
  input  B,
  input  in_6,
  output Equal,
  output A_2,
  output B_2
);

  wire and_2_out, and_3_out, xnor_1_out, xnor_2_out, xnor_3_out;

  and and_1 (Equal, xnor_1_out, xnor_2_out, xnor_3_out);
  xnor xnor_1 (xnor_1_out, ms, in_4);
  xnor xnor_2 (xnor_2_out, A, B);
  xnor xnor_3 (xnor_3_out, ls, in_6);
  and and_2 (and_2_out, xnor_1_out, A);
  and and_3 (and_3_out, xnor_1_out, xnor_2_out, ls);
  or or_1 (A_2, ms, and_2_out, and_3_out);
  not not_1 (B_2, A_2);
endmodule
