// Logisim project multiplexer.circ as structural Verilog: 1 circuit, main circuit main
module main (
  input  [2:0] XYZ,
  input  in_2,
  input  in_3,
  input  in_4,
  input  in_5,
  input  in_6,
  input  in_7,
  input  in_8,
  input  in_9,
  input  in_10,
  input  in_11,
  input  in_12,
  input  in_13,
  input  [1:0] YZ,
  input  in_15,
  input  in_16,
  input  in_17,
  input  X,
  input  in_19,
  output out_20,
  output out_21
);

  wire multiplexer_1_out, multiplexer_2_out;

  Multiplexer #(.select(2)) multiplexer_1 (
    .in0(in_10), .in1(in_11), .in2(in_12), .in3(in_13), .out(multiplexer_1_out), .sel(YZ));  // open: en
  Multiplexer #(.select(2)) multiplexer_2 (
    .in0(in_15), .in1(in_16), .in2(in_17), .in3(in_19), .out(multiplexer_2_out), .sel(YZ));  // open: en
  Multiplexer #(.select(3)) multiplexer_3 (
    .in0(in_2), .in1(in_3), .in2(in_4), .in3(in_5), .in4(in_6), .in5(in_7), .in6(in_8), .in7(in_9),
    .out(out_20), .sel(XYZ));  // open: en
  Multiplexer #(.select(2)) multiplexer_4 (
    .in0(multiplexer_1_out), .in1(multiplexer_1_out), .in2(multiplexer_2_out), .in3(multiplexer_2_out),
    .out(out_21), .sel({2{X}}));  // open: en

  // Notes on the sheet:
  //   PART A
  //   8:1 MUX
endmodule
