// Logisim project flip-flops.circ as structural Verilog: 1 circuit, main circuit main
module main (
  input  in_1,
  input  S,
  input  B,
  input  R,
  input  A,
  input  D,
  input  J,
  input  K,
  input  D_2,
  input  T,
  output out_11,
  output out_12,
  output out_13,
  output Q_prime,
  output Q_prime_2,
  output Q,
  output Q_2,
  output Q_prime_3,
  output Q_3,
  output Q_prime_4,
  output Q_4,
  output Q_5,
  output Q_6,
  output Q_prime_5,
  output Q_prime_6
);

  wire and_2_out, and_3_out, and_4_out, and_5_out, and_6_out, and_7_out, and_8_out, and_9_out, and_10_out,
       and_12_out, and_13_out, and_14_out, and_15_out, and_16_out, clock_1_out, clock_2_out, clock_3_out,
       clock_4_out, clock_5_out, clock_6_out, clock_7_out, not_1_out, not_2_out, not_3_out, not_4_out,
       not_5_out, not_6_out, not_7_out, not_8_out, not_9_out, not_10_out, not_11_out, not_12_out, not_13_out,
       not_14_out, not_15_out, not_16_out, not_17_out, not_18_out, not_19_out, or_2_out;

  Clock clock_1 (.out(clock_1_out));
  Clock clock_2 (.out(clock_2_out));
  Clock clock_3 (.out(clock_3_out));
  Clock clock_4 (.out(clock_4_out));
  Clock clock_5 (.out(clock_5_out));
  or or_1 (out_13, in_1, not_1_out);
  not not_1 (not_1_out, out_13);
  not not_2 (not_2_out, clock_2_out);
  not not_3 (not_3_out, clock_3_out);
  not not_4 (not_4_out, clock_4_out);
  not not_5 (not_5_out, D_2);
  not not_6 (not_6_out, clock_1_out);
  not not_7 (not_7_out, not_8_out);
  not not_8 (not_8_out, not_2_out);
  not not_9 (not_9_out, not_10_out);
  not not_10 (not_10_out, not_3_out);
  not not_11 (not_11_out, not_12_out);
  not not_12 (not_12_out, not_4_out);
  J_K_Flip_Flop j_k_ff_1 (
    .J(D_2), .clk(clock_5_out), .K(not_5_out), .Q(Q_5), .Qn(Q_prime_5));  // open: preset, en, reset
  and and_1 (out_11, not_6_out, clock_1_out);
  and and_2 (and_2_out, not_7_out, clock_2_out);
  and and_3 (and_3_out, not_9_out, clock_3_out);
  not not_13 (not_13_out, D);
  and and_4 (and_4_out, not_11_out, clock_4_out);
  and and_5 (and_5_out, S, and_2_out);
  and and_6 (and_6_out, and_2_out, R);
  and and_7 (and_7_out, D, and_3_out);
  and and_8 (and_8_out, and_3_out, not_13_out);
  and and_9 (and_9_out, J, Q_prime_4, and_4_out);
  and and_10 (and_10_out, and_4_out, Q_4, K);
  not not_14 (not_14_out, clock_6_out);
  Clock clock_6 (.out(clock_6_out));
  nor nor_1 (Q_prime, and_5_out, Q);
  nor nor_2 (Q, Q_prime, and_6_out);
  nor nor_3 (Q_prime_3, and_7_out, Q_3);
  nor nor_4 (Q_3, Q_prime_3, and_8_out);
  nor nor_5 (Q_prime_4, and_9_out, Q_4);
  nor nor_6 (Q_4, Q_prime_4, and_10_out);
  J_K_Flip_Flop j_k_ff_2 (.J(1'b1), .clk(T), .K(1'b1), .Q(Q_6), .Qn(Q_prime_6));  // open: preset, en, reset
  not not_15 (not_15_out, not_14_out);
  and and_11 (out_12, not_15_out, not_14_out);
  or or_2 (or_2_out, B, and_12_out);
  and and_12 (and_12_out, B, A);
  not not_16 (not_16_out, B);
  and and_13 (and_13_out, not_16_out, A);
  not not_17 (not_17_out, clock_7_out);
  Clock clock_7 (.out(clock_7_out));
  not not_18 (not_18_out, not_19_out);
  not not_19 (not_19_out, not_17_out);
  and and_14 (and_14_out, not_18_out, clock_7_out);
  and and_15 (and_15_out, or_2_out, and_14_out);
  and and_16 (and_16_out, and_14_out, and_13_out);
  nor nor_7 (Q_prime_2, and_15_out, Q_2);
  nor nor_8 (Q_2, Q_prime_2, and_16_out);

  // Notes on the sheet:
  //   Clock
  //   SR Flip Flop
  //   D Flip Flop
  //   JK Flip Flop
  //   JK Flip Flop as D Flip Flop
  //   Leading Edge Detector
  //   increase nots to increase duty cycle
  //   increase nots to increase period
  //   JK Flip Flop as T Flip Flop
  //   Trailing Edge Detector
  //   increase nots to increase duty cycle
  //   SR Flip Flop w/ Additional Logic
  //   S
  //   R
endmodule
