// Logisim project latches.circ as structural Verilog: 1 circuit, main circuit main
module main (
  input  R,
  input  S,
  input  R_2,
  input  S_prime,
  input  S_prime_2,
  input  S_2,
  input  R_prime,
  input  R_prime_2,
  input  S_3,
  input  D,
  input  G,
  input  G_2,
  input  R_3,
  output Q,
  output Q_prime,
  output Q_2,
  output Q_3,
  output Q_4,
  output Q_prime_2,
  output Q_prime_3,
  output Q_prime_4,
  output Q_5,
  output Q_6,
  output Q_prime_5,
  output Q_prime_6
);

  wire nand_1_out, nand_2_out, nand_5_out, nand_6_out, not_2_out, not_3_out, or_2_out;

  not not_1 (Q_prime, Q);
  or or_1 (Q, S, not_2_out);
  not not_2 (not_2_out, or_2_out);
  nand nand_1 (nand_1_out, S_3, G);
  nand nand_2 (nand_2_out, G, R_3);
  or or_2 (or_2_out, Q_prime, R);
  nor nor_1 (Q_2, R_2, Q_prime_2);
  nor nor_2 (Q_prime_2, Q_2, S_2);
  or or_3 (Q_5, ~nand_1_out, ~Q_prime_5);  // OR_Gate
  or or_4 (Q_prime_5, ~Q_5, ~nand_2_out);  // OR_Gate
  nand nand_3 (Q_3, S_prime, Q_prime_3);
  nand nand_4 (Q_prime_3, Q_3, R_prime);
  not not_3 (not_3_out, D);
  nand nand_5 (nand_5_out, D, G_2);
  nand nand_6 (nand_6_out, G_2, not_3_out);
  or or_5 (Q_4, ~S_prime_2, ~Q_prime_4);  // OR_Gate
  or or_6 (Q_prime_4, ~Q_4, ~R_prime_2);  // OR_Gate
  or or_7 (Q_6, ~nand_5_out, ~Q_prime_6);  // OR_Gate
  or or_8 (Q_prime_6, ~Q_6, ~nand_6_out);  // OR_Gate

  // Notes on the sheet:
  //   Basic Bistable SR Latch
  //   NOR SR Latch
  //   Gated SR Latch
  //   NAND SR Latch
  //   Gated D Latch
  //   OR SR Latch
endmodule
