// Logisim project left-shift.circ as structural Verilog: 1 circuit, main circuit main
module main (
  input  serial_in,
  input  async_enable,
  input  p_in_0,
  input  p_in_1,
  input  p_in_2,
  input  p_in_3,
  output p_out_0,
  output p_out_1,
  output p_out_2,
  output p_out_3,
  output serial_out
);

  wire and_1_out, and_2_out, and_3_out, and_4_out, and_5_out, and_6_out, and_7_out, and_8_out, clock_1_out,
       not_1_out, not_2_out, not_3_out, not_4_out;

  Clock clock_1 (.out(clock_1_out));
  and and_1 (and_1_out, async_enable, p_in_0);
  D_Flip_Flop d_ff_1 (
    .clk(clock_1_out), .D(serial_in), .Q(p_out_0), .preset(and_1_out), .reset(and_2_out));  // open: Qn, en
  and and_2 (and_2_out, not_1_out, async_enable);
  and and_3 (and_3_out, async_enable, p_in_1);
  not not_1 (not_1_out, p_in_0);
  D_Flip_Flop d_ff_2 (
    .clk(clock_1_out), .D(p_out_0), .Q(p_out_1), .preset(and_3_out), .reset(and_4_out));  // open: Qn, en
  and and_4 (and_4_out, not_2_out, async_enable);
  not not_2 (not_2_out, p_in_1);
  D_Flip_Flop d_ff_3 (
    .clk(clock_1_out), .D(p_out_1), .Q(p_out_2), .preset(and_6_out), .reset(and_5_out));  // open: Qn, en
  and and_5 (and_5_out, not_3_out, async_enable);
  and and_6 (and_6_out, async_enable, p_in_2);
  not not_3 (not_3_out, p_in_2);
  D_Flip_Flop d_ff_4 (
    .clk(clock_1_out), .D(p_out_2), .Q(p_out_3), .preset(and_8_out), .reset(and_7_out));  // open: Qn, en
  and and_7 (and_7_out, not_4_out, async_enable);
  and and_8 (and_8_out, async_enable, p_in_3);
  not not_4 (not_4_out, p_in_3);

  assign serial_out = p_out_3;
endmodule
