// Logisim project counter.circ as structural Verilog: 2 circuits, main circuit main
module main (
  input  x,
  input  reset,
  output _0,
  output _1,
  output _2,
  output _3
);

  wire _0_q, _1_q, _2_q, _3_q, clock_1_out, combinational_1_j0, combinational_1_j1, combinational_1_j2,
       combinational_1_j3, combinational_1_k0, combinational_1_k1, combinational_1_k2, combinational_1_k3;

  combinational combinational_1 (
    .x(x), .p0(_0_q), .p1(_1_q), .p2(_2_q), .p3(_3_q), .z0(_0), .z1(_1), .z2(_2), .z3(_3),
    .J0(combinational_1_j0), .J1(combinational_1_j1), .K1(combinational_1_k1), .J2(combinational_1_j2),
    .K2(combinational_1_k2), .J3(combinational_1_j3), .K3(combinational_1_k3), .K0(combinational_1_k0));
  Clock clock_1 (.out(clock_1_out));
  J_K_Flip_Flop u__0 (
    .J(combinational_1_j0), .clk(clock_1_out), .K(combinational_1_k0), .Q(_0_q), .reset(reset));  // open: Qn, preset, en
  J_K_Flip_Flop u__1 (
    .J(combinational_1_j1), .clk(clock_1_out), .K(combinational_1_k1), .Q(_1_q), .reset(reset));  // open: Qn, preset, en
  J_K_Flip_Flop u__2 (
    .J(combinational_1_j2), .clk(clock_1_out), .K(combinational_1_k2), .Q(_2_q), .reset(reset));  // open: Qn, preset, en
  J_K_Flip_Flop u__3 (
    .J(combinational_1_j3), .clk(clock_1_out), .K(combinational_1_k3), .Q(_3_q), .reset(reset));  // open: Qn, preset, en

  // Notes on the sheet:
  //   0
  //   1
  //   2
  //   3
endmodule

module combinational (
  input  x,
  input  p0,
  input  p1,
  input  p2,
  input  p3,
  output z3,
  output z2,
  output J0,
  output K0,
  output z1,
  output J1,
  output K1,
  output z0,
  output J2,
  output K2,
  output J3,
  output K3
);

  wire and_1_out, and_2_out, not_1_out, not_2_out, not_3_out, not_4_out, not_5_out, or_1_out, or_2_out,
       or_3_out, or_4_out, or_5_out, or_7_out, or_8_out, or_9_out, or_10_out, or_11_out, p0_prime_2_out,
       p0_prime_out, p1_p2_out, p1_p2_prime_out, p1_prime_out, p1_prime_p2_out, p1_prime_p2_prime_out,
       p2_2_out, p2_out, p2_prime_2_out, p2_prime_out, x_prime_out, x_prime_p0_out, x_prime_p0_prime_out,
       x_prime_p3_out;

  not not_1 (not_1_out, p0);
  not not_2 (not_2_out, x);
  not not_3 (not_3_out, p1);
  not not_4 (not_4_out, p3);
  not not_5 (not_5_out, p2);
  and x_p0 (J1, x, p0);
  and p1_prime_p2_prime (p1_prime_p2_prime_out, not_3_out, not_5_out);
  and x_p3_prime (J0, x, not_4_out);
  and x_prime_p0 (x_prime_p0_out, not_2_out, p0);
  and x_prime_p0_prime (x_prime_p0_prime_out, not_2_out, not_1_out);
  and p1_prime_p2 (p1_prime_p2_out, not_3_out, p2);
  and x_prime_p3 (x_prime_p3_out, not_2_out, p3);
  and p1_p2 (p1_p2_out, p1, p2);
  and p1_p2_prime (p1_p2_prime_out, p1, not_5_out);
  and u_p1 (J2, J1, p1);
  and u_p2 (p2_out, J1, p2);
  and p2_prime (p2_prime_out, J1, not_5_out);
  and p0_prime (p0_prime_out, J0, not_1_out);
  and and_1 (and_1_out, x_prime_p0_out, p1_prime_p2_prime_out);
  and p1_prime (p1_prime_out, x_prime_p0_prime_out, not_3_out);
  and p2_2 (p2_2_out, x_prime_p0_prime_out, p2);
  and p2_prime_2 (p2_prime_2_out, x_prime_p0_prime_out, not_5_out);
  and x_prime (x_prime_out, p1_prime_p2_out, not_2_out);
  and p0_prime_2 (p0_prime_2_out, p1_prime_p2_out, not_1_out);
  and and_2 (and_2_out, p0_prime_out, p1_prime_p2_prime_out);
  and p2_3 (J3, J2, p2);
  or or_1 (or_1_out, p0_prime_2_out, p2_prime_out);
  or or_2 (or_2_out, and_2_out, and_1_out);
  or or_3 (or_3_out, p1_prime_out, p1_prime_p2_out);
  or or_4 (or_4_out, p1_prime_p2_prime_out, p1_prime_out);
  or or_5 (or_5_out, or_1_out, x_prime_out);
  or or_6 (z3, or_5_out, p1_p2_prime_out);
  or or_7 (or_7_out, or_2_out, p2_out);
  or or_8 (or_8_out, or_7_out, x_prime_p3_out);
  or or_9 (or_9_out, or_3_out, p3);
  or or_10 (or_10_out, or_9_out, p2_2_out);
  or or_11 (or_11_out, or_4_out, p2_prime_2_out);
  or or_12 (z0, or_11_out, J2);
  or or_13 (z2, or_8_out, p1_p2_out);
  or or_14 (z1, or_10_out, J2);

  assign K0 = x;
  assign K1 = J1;
  assign K2 = J2;
  assign K3 = x;
endmodule
