// Logisim project Elevator.circ as structural Verilog: 2 circuits, main circuit main
module main (
  input  Up,
  input  Down,
  input  reset
);

  wire clock_1_out, combinational_1_d0, combinational_1_d1, combinational_1_d2, combinational_1_d3,
       combinational_1_door, combinational_1_floor_0, combinational_1_floor_1, D0_q, D1_q, D2_q, D3_q,
       n7_segment_display_driver_1_p5, n7_segment_display_driver_1_p6, n7_segment_display_driver_1_p7,
       n7_segment_display_driver_1_p8, n7_segment_display_driver_1_p9, n7_segment_display_driver_1_p10,
       n7_segment_display_driver_1_p11;

  Combinational combinational_1 (
    .Door(combinational_1_door), .Floor_1(combinational_1_floor_1), .Floor_0(combinational_1_floor_0),
    .D0(combinational_1_d0), .D1(combinational_1_d1), .D2(combinational_1_d2), .D3(combinational_1_d3),
    .P3(D3_q), .P2(D2_q), .P1(D1_q), .P0(D0_q), .Down(Down), .Up(Up));
  Clock clock_1 (.out(clock_1_out));
  D_Flip_Flop D0 (.clk(clock_1_out), .D(combinational_1_d0), .Q(D0_q), .preset(reset));  // open: Qn, en, reset
  D_Flip_Flop D1 (.clk(clock_1_out), .D(combinational_1_d1), .Q(D1_q), .preset(reset));  // open: Qn, en, reset
  D_Flip_Flop D2 (.clk(clock_1_out), .D(combinational_1_d2), .Q(D2_q), .reset(reset));  // open: Qn, preset, en
  D_Flip_Flop D3 (.clk(clock_1_out), .D(combinational_1_d3), .Q(D3_q), .reset(reset));  // open: Qn, preset, en
  // _7_segment_display_driver 7_segment_display_driver_1: pin names not known; wires that end beside it: 1'b0, 1'b0, combinational_1_floor_1, combinational_1_floor_0, n7_segment_display_driver_1_p5, n7_segment_display_driver_1_p6, n7_segment_display_driver_1_p7, n7_segment_display_driver_1_p8, n7_segment_display_driver_1_p9, n7_segment_display_driver_1_p10, n7_segment_display_driver_1_p11
  _7_Segment_Display u_7_segment_display_1 (
    .g(n7_segment_display_driver_1_p11), .f(n7_segment_display_driver_1_p10),
    .a(n7_segment_display_driver_1_p5), .b(n7_segment_display_driver_1_p6),
    .e(n7_segment_display_driver_1_p9), .d(n7_segment_display_driver_1_p8),
    .c(n7_segment_display_driver_1_p7), .dp(combinational_1_door));
endmodule

module Combinational (
  input  P3,
  input  P2,
  input  P1,
  input  P0,
  input  Down,
  input  Up,
  output Door,
  output Floor_1,
  output Floor_0,
  output D0,
  output D1,
  output D2,
  output D3
);

  wire and_1_out, and_2_out, and_3_out, and_4_out, and_5_out, and_6_out, and_7_out, and_8_out, and_9_out,
       and_10_out, and_11_out, and_12_out, and_13_out, and_14_out, and_15_out, and_16_out, and_17_out,
       and_18_out, and_19_out, and_20_out, and_21_out, and_22_out, and_23_out, and_24_out, and_25_out,
       and_26_out, and_27_out, not_1_out, not_2_out, not_3_out, not_4_out, not_5_out, not_6_out, or_1_out,
       or_2_out, or_3_out, or_4_out, or_5_out, or_6_out, or_7_out, or_8_out, or_9_out, or_10_out, or_11_out,
       or_12_out, or_15_out;

  not not_1 (not_1_out, P2);
  not not_2 (not_2_out, P1);
  not not_3 (not_3_out, P3);
  not not_4 (not_4_out, Up);
  not not_5 (not_5_out, Down);
  not not_6 (not_6_out, P0);
  and and_1 (and_1_out, not_5_out, P1, P2, not_3_out);
  and and_2 (and_2_out, not_5_out, not_4_out, not_2_out, not_3_out);
  and and_3 (and_3_out, not_6_out, P2, not_3_out);
  and and_4 (and_4_out, not_4_out, not_1_out);
  and and_5 (and_5_out, not_1_out, P3);
  and and_6 (and_6_out, not_6_out, P2);
  and and_7 (and_7_out, P2, not_3_out);
  and and_8 (and_8_out, not_6_out, not_3_out);
  and and_9 (and_9_out, P1, P2, not_3_out);
  and and_10 (and_10_out, not_2_out, P3);
  and and_11 (and_11_out, not_1_out, P3);
  and and_12 (and_12_out, P0, not_1_out);
  and and_13 (and_13_out, not_5_out, P1, P2, not_3_out);
  and and_14 (and_14_out, not_6_out, P2, not_3_out);
  and and_15 (and_15_out, not_4_out, P0, not_1_out);
  and and_16 (and_16_out, not_4_out, not_2_out, not_3_out);
  and and_17 (and_17_out, not_1_out, P3);
  and and_18 (and_18_out, P1, P2, not_3_out);
  and and_19 (and_19_out, not_2_out, P3);
  and and_20 (and_20_out, not_1_out, P3);
  and and_21 (and_21_out, P0, P1);
  and and_22 (and_22_out, not_6_out, P2);
  and and_23 (and_23_out, P2, not_3_out);
  and and_24 (and_24_out, not_6_out, not_3_out);
  and and_25 (and_25_out, Down, P0, P2);
  and and_26 (and_26_out, Up, P0, not_2_out);
  and and_27 (and_27_out, P0, P3);
  or or_1 (or_1_out, and_7_out, and_8_out);
  or or_2 (or_2_out, and_9_out, and_10_out);
  or or_3 (or_3_out, and_11_out, and_12_out);
  or or_4 (or_4_out, and_14_out, and_15_out);
  or or_5 (or_5_out, and_16_out, and_17_out);
  or or_6 (or_6_out, and_18_out, and_19_out);
  or or_7 (or_7_out, and_20_out, and_21_out);
  or or_8 (or_8_out, and_23_out, and_24_out);
  or or_9 (or_9_out, and_26_out, and_27_out);
  or or_10 (or_10_out, and_1_out, or_11_out);
  or or_11 (or_11_out, and_2_out, and_3_out);
  or or_12 (or_12_out, and_4_out, and_5_out);
  or or_13 (Floor_1, and_6_out, or_1_out);
  or or_14 (Floor_0, or_2_out, or_3_out);
  or or_15 (or_15_out, or_4_out, or_5_out);
  or or_16 (D1, or_6_out, or_7_out);
  or or_17 (D2, and_22_out, or_8_out);
  or or_18 (D3, and_25_out, or_9_out);
  or or_19 (Door, or_10_out, or_12_out);
  or or_20 (D0, and_13_out, or_15_out);

  // Notes on the sheet:
  //   p3
  //   p2
  //   p1
  //   p0
  //   up
  //   down
endmodule
